# Fritzing sketch Terry Controller (saved by Fritzing 0.9.3b)

parts:
  Part1 = Thumb Joystick
  Part2 = Thumb Joystick
  Part3 = NRF24L01+ Breakout Board
  Part4 = Arduino Nano (Rev3.0)
  VCC1 = Battery block 9V  # not connected

nets:
  N1: Part1.HORZ, Part4.A0
  N2: Part1.VERT, Part4.A1
  N3: Part2.HORZ, Part4.A2
  N4: Part2.VERT, Part4.A3
  VCC: Part3.VCC, Part4.3V3
  N5: Part3.CE, Part4.D9
  N6: Part3.CS, Part4.D10
  N7: Part3.SCK, Part4.D13/SCK
  N8: Part3.MOSI, Part4.D11/MOSI
  N9: Part3.MISO, Part4.D12/MISO
