# Fritzing sketch Terry's Car (saved by Fritzing 0.9.3b)

parts:
  Part1 = Arduino Uno (Rev3)
  M2 = DC Motor
  S1 = H-Bridge with L298N
  M1 = DC Motor
  Part2 = NRF24L01+ Breakout Board
  IR1 = TSOP312.., 314.. [package=THT]
  IR2 = TSOP312.., 314.. [package=THT]
  VCC1 = Battery block 9V

nets:
  N1: Part1.D8, IR1.Data
  N2: Part1.D9_PWM, Part2.CE
  N3: Part1.D10_PWM/SS, Part2.CS
  N4: Part1.D11_PWM/MOSI, Part2.MOSI
  N5: Part1.D12/MISO, Part2.MISO
  N6: Part1.D13/SCK, Part2.SCK
  GND: Part1.GND, S1.GND, Part2.GND, VCC1.-
  N7: Part1.D2, S1.IN4
  N8: Part1.D3_PWM, S1.IN3
  N9: Part1.D4, S1.IN2
  N10: Part1.D5_PWM, S1.IN1
  N11: Part1.D7, IR2.Data
  3V3: Part1.3V3, Part2.VCC
  VIN: Part1.VIN, S1.5V
  N12: M2.pin_1, S1.M1-02
  N13: M2.pin_2, S1.M1-01
  N14: S1.12V, VCC1.+
  N15: S1.ENA, S1.ENA-5V
  N16: S1.ENB, S1.ENB-5V
  N17: S1.M2-01, M1.pin_2
  N18: S1.M2-02, M1.pin_1

custom parts:
  H-Bridge with L298N: h-bridge
